# Fritzing sketch fritzingFile (saved by Fritzing 0.9.4)
breadboards: 3

parts:
  R1 = Rotary Potentiometer (Small) [maximum_resistance=100kΩ package=THT]
  LCD1 = LCD screen
  Componente1 = Arduino Nano (Rev3.0)
  LED1 = LED - 5mm [color="Red (633nm)" package="5 mm [THT]"]
  LED2 = LED - 5mm [color="Green (555nm)" package="5 mm [THT]"]
  S1 = Pushbutton [package="[THT]"]
  S2 = Pushbutton [package="[THT]"]
  R2 = Resistor [tolerance=±5% resistance=220 package=THT]
  R3 = Resistor [tolerance=±5% resistance=220 package=THT]
  R4 = Resistor [tolerance=±5% resistance=10k package=THT]
  R5 = Resistor [tolerance=±5% resistance=10k package=THT]

nets:
  VSS: R1.leg1, LCD1.VSS, LCD1.R/W, LCD1.LED-, Componente1.GND, LED1.cathode, LED2.cathode, R4.Pin_0, R5.Pin_0
  N1: R1.wiper, LCD1.V0
  VDD: R1.leg2, LCD1.VDD, LCD1.LED+, Componente1.5V, S1.Pin_1, S1.Pin_2, S2.Pin_1, S2.Pin_2
  N2: LCD1.RS, Componente1.D12/MISO
  N3: LCD1.E, Componente1.D11/MOSI
  N4: LCD1.DB4, Componente1.D5
  N5: LCD1.DB5, Componente1.D4
  N6: LCD1.DB6, Componente1.D3
  N7: LCD1.DB7, Componente1.D2
  N8: Componente1.D7, S2.Pin_3, S2.Pin_4, R4.Pin_1
  N9: Componente1.D8, S1.Pin_3, S1.Pin_4, R5.Pin_1
  N10: Componente1.D9, R3.Pin_1
  N11: Componente1.D10, R2.Pin_1
  N12: LED1.anode, R2.Pin_0
  N13: LED2.anode, R3.Pin_0
